# Fritzing sketch LOLIN32 (saved by Fritzing 0.9.3b)
circuit board: 6.02668cm x 3.89598cm
breadboards: 2

parts:
  SP1 = SPEAKER [package=pcb_mount_speaker]
  U2 = LM2596 step down module
  VIN = male pin header, 2 pins [form="♂ (male)"]
  Speaker_B_R = male pin header, 2 pins [form="♂ (male)"]
  Headphones_S_G_L_R = male pin header, 4 pins [form="♂ (male)"]
  Buttons_+_-_P = male pin header, 3 pins [form="♂ (male)"]
  GND = male pin header, 3 pins [form="♂ (male)"]
  GND_5V = male pin header, 2 pins [form="♂ (male)"]
  5V_VIN_B = male pin header, 2 pins [form="♂ (male)"]
  5V_VIN_C = male pin header, 2 pins [form="♂ (male)"]
  MMA845X_/_HY-M323 = male pin header, 8 pins [form="♂ (male)"]
  RFID-RC522 = RFID-RC522-v2
  LEDs_-_D_C_+ = male pin header, 4 pins [form="♂ (male)"]
  LOLIN32 = lolin
  IRLML6402 = MOSFET-PCHANNEL [package=sot23-3]
  R(50-100) = Resistor [tolerance=±5% resistance=68 package=THT]
  DFUSB_D+_D- = male pin header, 2 pins [form="♂ (male)"]
  ESPUSB_OUT = male pin header, 2 pins [form="♂ (male)"]
  ESPUSB_D+_D-_IN = male pin header, 2 pins [form="♂ (male)"]
  DFPlayer = DFRobot DFPlayer Mini [part_number=DFR0299]
  DFPlayer_A_(VCC) = male pin header, 8 pins [form="♂ (male)"]
  (BSY)_DFPlayer_B = male pin header, 8 pins [form="♂ (male)"]
  RFID-RC522_2 = male pin header, 8 pins [form="♂ (male)"]
  R33k_4_2V_A = Resistor [tolerance=±5% resistance=33k package=THT]
  R33k_4_2V_B = Resistor [tolerance=±5% resistance=33k package=THT]
  R100k_4_2V_C = Resistor [tolerance=±5% resistance=100k package=THT]
  R33k_5V_A = Resistor [tolerance=±5% resistance=33k package=THT]
  R33k_5V_B = Resistor [tolerance=±5% resistance=33k package=THT]
  R100k_5V_C = Resistor [tolerance=±5% resistance=100k package=THT]
  Lipo_4_2V_+ = male pin header, 1 pin [form="♂ (male)"]

nets:
  N1: SP1.+, Speaker_B_R.pin1, DFPlayer.SPK_1, DFPlayer_A_(VCC).pin6
  N2: SP1.-, Speaker_B_R.pin2, DFPlayer.SPK_2, DFPlayer_A_(VCC).pin8
  N3: U2.IN+, VIN.pin2
  N4: U2.IN-, U2.OUT-, VIN.pin1, Headphones_S_G_L_R.pin3, GND.pin1, GND.pin2, GND.pin3, GND_5V.pin1, 5V_VIN_B.pin1, 5V_VIN_C.pin1, MMA845X_/_HY-M323.pin3, RFID-RC522.GND, LEDs_-_D_C_+.pin4, LOLIN32.connector15, LOLIN32.connector20, LOLIN32.connector30, LOLIN32.connector31, LOLIN32.connector37, DFPlayer.GND-1, DFPlayer.GND-2, DFPlayer_A_(VCC).pin7, (BSY)_DFPlayer_B.pin7, RFID-RC522_2.pin3, R100k_4_2V_C.Pin_0, R100k_5V_C.Pin_0
  N5: U2.OUT+, GND_5V.pin2, 5V_VIN_B.pin2, 5V_VIN_C.pin2, LOLIN32.connector14, R33k_5V_A.Pin_1
  N6: Headphones_S_G_L_R.pin1, DFPlayer.DAC_L, DFPlayer_A_(VCC).pin5
  N7: Headphones_S_G_L_R.pin2, DFPlayer.DAC_R, DFPlayer_A_(VCC).pin4
  N8: Headphones_S_G_L_R.pin4, LOLIN32.connector19
  N9: Buttons_+_-_P.pin1, LOLIN32.connector8
  N10: Buttons_+_-_P.pin2, LOLIN32.connector9
  N11: Buttons_+_-_P.pin3, LOLIN32.connector10
  3.3V: MMA845X_/_HY-M323.pin1, RFID-RC522.3.3V, LEDs_-_D_C_+.pin1, IRLML6402.D, DFPlayer.VCC, DFPlayer_A_(VCC).pin1, RFID-RC522_2.pin1
  N12: MMA845X_/_HY-M323.pin4, LOLIN32.connector33
  N13: MMA845X_/_HY-M323.pin5, LOLIN32.connector32
  N14: RFID-RC522.SDA, LOLIN32.connector21, RFID-RC522_2.pin8
  N15: RFID-RC522.SCK, LOLIN32.connector27, RFID-RC522_2.pin7
  N16: RFID-RC522.MOSI, LOLIN32.connector28, RFID-RC522_2.pin6
  N17: RFID-RC522.MISO, LOLIN32.connector29, RFID-RC522_2.pin5
  N18: RFID-RC522.IRQ, RFID-RC522_2.pin4
  N19: RFID-RC522.RST, LOLIN32.connector22, RFID-RC522_2.pin2
  N20: LEDs_-_D_C_+.pin2, LOLIN32.connector12
  N21: LEDs_-_D_C_+.pin3, LOLIN32.connector13
  N22: LOLIN32.connector0, LOLIN32.connector34, IRLML6402.S
  N23: LOLIN32.connector4, DFPlayer.BUSY, (BSY)_DFPlayer_B.pin1
  N24: LOLIN32.connector5, R(50-100).Pin_1
  N25: LOLIN32.connector6, R33k_5V_B.Pin_0, R100k_5V_C.Pin_1
  N26: LOLIN32.connector7, R33k_4_2V_B.Pin_0, R100k_4_2V_C.Pin_1
  N27: LOLIN32.connector18, DFPlayer.IO_1, (BSY)_DFPlayer_B.pin8
  N28: LOLIN32.connector23, DFPlayer.TX, DFPlayer_A_(VCC).pin3
  N29: LOLIN32.connector24, DFPlayer.RX, DFPlayer_A_(VCC).pin2
  N30: IRLML6402.G, R(50-100).Pin_0
  N31: DFUSB_D+_D-.pin1, DFPlayer.USB_POS, (BSY)_DFPlayer_B.pin3
  N32: DFUSB_D+_D-.pin2, DFPlayer.USB_NEG, (BSY)_DFPlayer_B.pin2
  N33: ESPUSB_OUT.pin1, ESPUSB_D+_D-_IN.pin1
  N34: ESPUSB_OUT.pin2, ESPUSB_D+_D-_IN.pin2
  N35: DFPlayer.IO_2, (BSY)_DFPlayer_B.pin6
  N36: DFPlayer.ADKEY_1, (BSY)_DFPlayer_B.pin5
  N37: DFPlayer.ADKEY_2, (BSY)_DFPlayer_B.pin4
  N38: R33k_4_2V_A.Pin_0, R33k_4_2V_B.Pin_1
  N39: R33k_4_2V_A.Pin_1, Lipo_4_2V_+.pin1
  N40: R33k_5V_A.Pin_0, R33k_5V_B.Pin_1

custom parts:
  LM2596 step down module: LM2596 DC-DC step down power supply module 3 A.
  RFID-RC522-v2: A simple China made RFID-RC522 Reader; do check the pin labels, as this is a MFRC522 based clone.
